// Logisim project MpMp25.circ as structural Verilog: 6 circuits, main circuit MAIN
module MAIN (
  input  RST
);

  wire ALU_F_E, and_2_out, and_3_out, and_4_out, and_5_out, CLK, CLK_E, clock_1_out, comparator_1_eq,
       cu_1_alu_accue, cu_1_alu_ce, cu_1_clk_qtr, cu_1_i3_to_alu, cu_1_lng_jmp_i, cu_1_lng_jmp_r,
       cu_1_rf_ce0, cu_1_rf_ce1, cu_1_rf_ptr_e, cu_1_rf_w_nr, decoder_1_out0, decoder_1_out1, decoder_1_out2,
       decoder_1_out3, decoder_1_out4, decoder_1_out5, decoder_1_out6, decoder_2_out0, decoder_2_out1,
       decoder_2_out7, decoder_3_out0, decoder_3_out1, decoder_3_out2, decoder_3_out3, decoder_3_out4,
       decoder_3_out5, IO_E, nor_1_out, PC_OVF, RAM_CE, RAM_WE, RF_BUS_0_E, rgb_video_1_p2;
  wire [0:0] keyboard_1_avail;
  wire [2:0] cu_1_reg0, cu_1_reg1;
  wire [3:0] cu_1_alu_cmd, joystick_1_x, joystick_1_y;
  wire [3:3] cu_1_const_2;
  wire [6:0] cu_1_const, keyboard_1_data;
  wire [7:0] Addr, alu_1_flags_out, alu_1_result, ALU_F_IN, controlled_buffer_4_out,
       controlled_buffer_11_out, DBG_LED, IO_8_B_q, IO_9_G_q, IO_a_r_q, IO_D_X_q, IO_F_Y_q, Mem_Page, PC,
       ram_1_dout, register_2_q, Sprite_memory_data;
  wire [15:0] Program_memory_data, register_1_q;

  Clock clock_1 (.out(clock_1_out));
  and and_1 (CLK, ~CLK_E, clock_1_out);  // AND_Gate
  CU cu_1 (
    .CLK(CLK), .RST(RST), .Instruction(Program_memory_data), .ALU_F_IN(ALU_F_IN), .Reg0(cu_1_reg0),
    .Reg1(cu_1_reg1), .Const({cu_1_const_2[3], cu_1_const}), .RF_W_nR(cu_1_rf_w_nr), .RF_CE0(cu_1_rf_ce0),
    .RF_CE1(cu_1_rf_ce1), .ALU_AccuE(cu_1_alu_accue), .ALU_CE(cu_1_alu_ce), .ALU_CMD(cu_1_alu_cmd),
    .RAM_WE(RAM_WE), .RAM_CE(RAM_CE), .RF_PTR_E(cu_1_rf_ptr_e), .CLK_QTR(cu_1_clk_qtr),
    .RF_DATAOUT_O_E(RF_BUS_0_E), .IO_E(IO_E), .Addr(Addr), .ALU_F_E(ALU_F_E), .LNG_JMP_I(cu_1_lng_jmp_i),
    .LNG_JMP_R(cu_1_lng_jmp_r), .I3_TO_ALU(cu_1_i3_to_alu));
  assign Addr = cu_1_lng_jmp_i ? 8'hf9 : 8'bz;  // Controlled_Buffer controlled_buffer_1
  assign Addr = cu_1_lng_jmp_r ? 8'hf9 : 8'bz;  // Controlled_Buffer controlled_buffer_2
  assign {cu_1_const_2[3], cu_1_const} = cu_1_lng_jmp_i ? {{5{1'b0}}, cu_1_reg0} : 8'bz;  // Controlled_Buffer controlled_buffer_3
  Register #(.width(16)) register_1 (.Q(register_1_q));  // open: D, en, clk, clr
  assign controlled_buffer_4_out = cu_1_i3_to_alu ? {{5{1'b0}}, cu_1_reg0} : 8'bz;  // Controlled_Buffer controlled_buffer_4
  Comparator #(.width(16)) comparator_1 (.a(register_1_q), .b({Mem_Page, PC}), .eq(comparator_1_eq));  // open: gt, lt
  Hex_Digit_Display hex_digit_display_1 (.value(register_1_q[15:12]));  // open: dp
  // Switch switch_1: pin names not known; wires that end beside it: comparator_1_eq, CLK_E
  Pull_Resistor pull_resistor_1 (.node(CLK_E));
  Hex_Digit_Display hex_digit_display_2 (.value(register_1_q[11:8]));  // open: dp
  Hex_Digit_Display hex_digit_display_3 (.value(register_1_q[7:4]));  // open: dp
  Hex_Digit_Display hex_digit_display_4 (.value(Mem_Page[7:4]));  // open: dp
  Hex_Digit_Display hex_digit_display_5 (.value(Mem_Page[3:0]));  // open: dp
  Hex_Digit_Display hex_digit_display_6 (.value(register_1_q[3:0]));  // open: dp
  Hex_Digit_Display hex_digit_display_7 (.value(PC[7:4]));  // open: dp
  Hex_Digit_Display hex_digit_display_8 (.value(PC[3:0]));  // open: dp
  RF rf_1 (
    .Addr0(cu_1_reg0), .Addr1(cu_1_reg1), .Data_In({cu_1_const_2[3], cu_1_const}), .W_nR(cu_1_rf_w_nr),
    .CE0(cu_1_rf_ce0), .CE1(cu_1_rf_ce1), .CLK(CLK), .RST(RST), .PTR_E(cu_1_rf_ptr_e),
    .CLK_QTR(cu_1_clk_qtr), .Data_Out0(controlled_buffer_4_out), .Data_Out1({cu_1_const_2[3], cu_1_const}),
    .PC(PC), .Pointer(Addr), .PC_OVF(PC_OVF));
  // LedBar #(.inputtype("row")) ledbar_1: pin names not known; wires that end beside it: DBG_LED
  and and_2 (and_2_out, Addr[3], ~Addr[4], ~Addr[5], ~Addr[6], ~Addr[7], IO_E);  // AND_Gate
  and and_3 (and_3_out, Addr[3], Addr[4], Addr[5], Addr[6], Addr[7], IO_E);
  ALU alu_1 (
    .CMD_15_12(cu_1_alu_cmd), .OP0(controlled_buffer_4_out), .OP1({cu_1_const_2[3], cu_1_const}),
    .Flags_in(ALU_F_IN), .Flags_out(alu_1_flags_out), .Result(alu_1_result));
  and and_4 (and_4_out, ~Addr[3], ~Addr[4], ~Addr[5], ~Addr[6], ~Addr[7], IO_E);  // AND_Gate
  Hex_Digit_Display Y (.value(joystick_1_y));  // open: dp
  Hex_Digit_Display X (.value(joystick_1_x));  // open: dp
  Joystick joystick_1 (.x(joystick_1_x), .y(joystick_1_y));
  Decoder #(.select(3)) decoder_1 (
    .out0(decoder_1_out0), .out1(decoder_1_out1), .out2(decoder_1_out2), .out3(decoder_1_out3),
    .out4(decoder_1_out4), .out5(decoder_1_out5), .out6(decoder_1_out6), .sel(Addr[2:0]), .en(and_2_out));  // open: out7
  Decoder #(.select(3)) decoder_2 (
    .out0(decoder_2_out0), .out1(decoder_2_out1), .out7(decoder_2_out7), .sel(Addr[2:0]), .en(and_3_out));  // open: out2, out3, out4, out5, out6
  assign {cu_1_const_2[3], cu_1_const} = cu_1_alu_ce ? register_2_q : 8'bz;  // Controlled_Buffer controlled_buffer_5
  Register register_2 (.D(alu_1_result), .en(cu_1_alu_accue), .Q(register_2_q), .clk(CLK), .clr(RST));
  Decoder #(.select(3)) decoder_3 (
    .out0(decoder_3_out0), .out1(decoder_3_out1), .out2(decoder_3_out2), .out3(decoder_3_out3),
    .out4(decoder_3_out4), .out5(decoder_3_out5), .sel(Addr[2:0]), .en(and_4_out));  // open: out6, out7
  LED led_1 (.in(decoder_3_out5));
  assign {cu_1_const_2[3], cu_1_const} = decoder_3_out5 ? {joystick_1_y, joystick_1_x} : 8'bz;  // Controlled_Buffer controlled_buffer_6
  TTY tty_1 (.data(cu_1_const), .clk(CLK), .we(decoder_3_out0), .clr(decoder_3_out1));
  RAM ram_1 (.addr(Addr), .we(RAM_WE), .oe(CLK), .clk(CLK), .din({cu_1_const_2[3], cu_1_const}), .dout(ram_1_dout));
  Register register_3 (.D(alu_1_flags_out), .en(cu_1_alu_accue), .Q(ALU_F_IN), .clk(CLK), .clr(RST));
  nor nor_1 (nor_1_out, and_4_out, and_2_out, and_3_out);
  assign {cu_1_const_2[3], cu_1_const} = decoder_3_out2 ? {1'b0, keyboard_1_data} : 8'bz;  // Controlled_Buffer controlled_buffer_7
  assign {cu_1_const_2[3], cu_1_const} = decoder_3_out3 ? {{7{1'b0}}, keyboard_1_avail[0]} : 8'bz;  // Controlled_Buffer controlled_buffer_8
  assign {cu_1_const_2[3], cu_1_const} = RF_BUS_0_E ? controlled_buffer_4_out : 8'bz;  // Controlled_Buffer controlled_buffer_9
  assign {cu_1_const_2[3], cu_1_const} = RAM_CE ? ram_1_dout : 8'bz;  // Controlled_Buffer controlled_buffer_10
  Hex_Digit_Display hex_digit_display_9 (.value({cu_1_const_2[3], cu_1_const[6:4]}));  // open: dp
  assign controlled_buffer_11_out = decoder_2_out7 ? {cu_1_const_2[3], cu_1_const} : 8'bz;  // Controlled_Buffer controlled_buffer_11
  Pull_Resistor pull_resistor_2 (.node(controlled_buffer_11_out));
  Hex_Digit_Display hex_digit_display_10 (.value(cu_1_const[3:0]));  // open: dp
  Register IO_8_B (.D({cu_1_const_2[3], cu_1_const}), .en(decoder_1_out0), .Q(IO_8_B_q), .clk(CLK), .clr(RST));
  Register IO_9_G (.D({cu_1_const_2[3], cu_1_const}), .en(decoder_1_out1), .Q(IO_9_G_q), .clk(CLK), .clr(RST));
  Register IO_a_r (.D({cu_1_const_2[3], cu_1_const}), .en(decoder_1_out2), .Q(IO_a_r_q), .clk(CLK), .clr(RST));
  Register IO_D_X (.D({cu_1_const_2[3], cu_1_const}), .en(decoder_1_out5), .Q(IO_D_X_q), .clk(CLK), .clr(RST));
  Register IO_F_Y (.D({cu_1_const_2[3], cu_1_const}), .en(decoder_1_out6), .Q(IO_F_Y_q), .clk(CLK), .clr(RST));
  Counter #(.trigger("falling")) counter_1 (
    .load(decoder_2_out1), .D({cu_1_const_2[3], cu_1_const}), .count(PC_OVF), .Q(Mem_Page), .up(1'b1),
    .clk(CLK), .clr(RST));  // open: carry
  S_R_Flip_Flop s_r_ff_1 (
    .S(controlled_buffer_11_out[0]), .clk(CLK), .R(RST), .Q(DBG_LED[0]));  // open: Qn, preset, reset
  S_R_Flip_Flop s_r_ff_2 (
    .S(controlled_buffer_11_out[1]), .clk(CLK), .R(RST), .Q(DBG_LED[1]));  // open: Qn, preset, reset
  S_R_Flip_Flop s_r_ff_3 (
    .S(controlled_buffer_11_out[2]), .clk(CLK), .R(RST), .Q(DBG_LED[2]));  // open: Qn, preset, reset
  S_R_Flip_Flop s_r_ff_4 (
    .S(controlled_buffer_11_out[3]), .clk(CLK), .R(RST), .Q(DBG_LED[3]));  // open: Qn, preset, reset
  S_R_Flip_Flop s_r_ff_5 (
    .S(controlled_buffer_11_out[4]), .clk(CLK), .R(RST), .Q(DBG_LED[4]));  // open: Qn, preset, reset
  S_R_Flip_Flop s_r_ff_6 (
    .S(controlled_buffer_11_out[5]), .clk(CLK), .R(RST), .Q(DBG_LED[5]));  // open: Qn, preset, reset
  S_R_Flip_Flop s_r_ff_7 (
    .S(controlled_buffer_11_out[6]), .clk(CLK), .R(RST), .Q(DBG_LED[6]));  // open: Qn, preset, reset
  S_R_Flip_Flop s_r_ff_8 (
    .S(controlled_buffer_11_out[7]), .clk(CLK), .R(RST), .Q(DBG_LED[7]));  // open: Qn, preset, reset
  // RGB_Video #(.cursor("No Cursor"), .height(256), .scale(3), .width(256)) rgb_video_1: pin names not known; wires that end beside it: IO_8_B_q, rgb_video_1_p2, CLK, decoder_1_out3, IO_D_X_q, IO_F_Y_q, {IO_a_r_q, IO_9_G_q, IO_8_B_q}
  or or_1 (rgb_video_1_p2, decoder_1_out4, RST);
  assign {cu_1_const_2[3], cu_1_const} = decoder_2_out0 ? Mem_Page : 8'bz;  // Controlled_Buffer controlled_buffer_12
  Hex_Digit_Display hex_digit_display_11 (.value(IO_D_X_q[7:4]));  // open: dp
  Hex_Digit_Display hex_digit_display_12 (.value(IO_D_X_q[3:0]));  // open: dp
  Hex_Digit_Display hex_digit_display_13 (.value(IO_F_Y_q[7:4]));  // open: dp
  Keyboard keyboard_1 (
    .clk(CLK), .re(decoder_3_out2), .clr(decoder_3_out4), .avail(keyboard_1_avail[0]), .data(keyboard_1_data));
  Hex_Digit_Display hex_digit_display_14 (.value(IO_F_Y_q[3:0]));  // open: dp
  ROM #(.addrWidth(16), .dataWidth(16)) Program_memory (.addr({Mem_Page, PC}), .data(Program_memory_data));
  ROM Sprite_memory (.addr(Addr), .data(Sprite_memory_data));
  and and_5 (and_5_out, nor_1_out, IO_E);
  assign {cu_1_const_2[3], cu_1_const} = and_5_out ? Sprite_memory_data : 8'bz;  // Controlled_Buffer controlled_buffer_13

  // Notes on the sheet:
  //   Data Bus
  //   Instruction Bus
  //   CE
  //   Reset
  //   W/E
  //   RGB 24 Bit
  //   X
  //   Y
  //   contents of Program_memory (hex, n*v repeats v):
  //   fa90 fb90 ff18 138 fe00 de0a de09 de08 de0c 8852 feff 708 feff de0a de09 fe00 de08 fc08 d538 fe08
  //   55e9 c819 da0d db0e db0b 12d1 16f1 b814 7f9 3d9 2d7 2d1 14e1 b812 13df 13d9 708 feff de0a de09 fe00
  //   de08 fc08 d538 fe08 55e9 c832 da0d db0e db0b 12d1 16f1 b82d 7f9 3d9 2d7 2d1 14e1 b82b 13df 13d9 ff30
  //   fc08 d538 fe08 55e9 c846 da0d db0e db0b 12d1 16f1 b841 7f9 3d9 2d7 2d1 14e1 b83f 13df 13d9 8903 fe00
  //   de0a de09 fec8 de08 fa28 fb28 fdb0 da0d db0e de0b 2d1 15e9 b85a fa28 3d9 fdb0 da0d db0e de0b 2d1
  //   15e9 b863 fa28 fbc8 fdb0 da0d db0e de0b 2d1 15e9 b86c fa28 3d9 fdb0 da0d db0e de0b 2d1 15e9 b875
  //   fa28 fb28 fda0 da0d db0e de0b 3d9 15e9 b87e fa29 fb28 fda0 da0d db0e de0b 3d9 15e9 b887 fad8 fb28
  //   fda0 da0d db0e de0b 3d9 15e9 b890 fad9 fb28 fda0 da0d db0e de0b 3d9 15e9 b899 fa3c fb3c fd88 da0d
  //   db0e de0b 2d1 15e9 b8a2 fa3c 3d9 fd88 da0d db0e de0b 2d1 15e9 b8ab fa3c fbb4 fd88 da0d db0e de0b 2d1
  //   15e9 b8b4 fa3c 3d9 fd88 da0d db0e de0b 2d1 15e9 b8bd fa80 fb3c fd32 da0d db0e de0b 3d9 15e9 b8c6
  //   fa81 fb3c fd32 da0d db0e de0b 3d9 15e9 b8cf fa80 fb96 fd1e da0d db0e de0b 3d9 15e9 b8d8 fa81 fb96
  //   fd1e da0d db0e de0b 3d9 15e9 b8e1 fa68 fb78 fd30 da0d db0e de0b 2d1 15e9 b8ea fa68 3d9 fd30 da0d
  //   db0e de0b 2d1 15e9 b8f3 feff de0a de09 fe00 de08 fa90 fb90 ff18 138 880a ef02 df04 17f8 9803 fe64
  //   157e 9814 fe77 157e 9836 fe61 157e 9858 fe73 157e 987a b803 fe00 ff30 de0a de09 de08 fc08 d538 fe08
  //   55e9 c821 da0d db0e db0b 12d1 16f1 b81c 7f9 3d9 2d7 2d1 14e1 b81a 13df 13d9 f910 510 5ef fcd7 176c
  //   a834 220 8824 228 8824 fe00 ff30 de0a de09 de08 fc08 d538 fe08 55e9 c843 da0d db0e db0b 12d1 16f1
  //   b83e 7f9 3d9 2d7 2d1 14e1 b83c 13df 13d9 f918 518 15ef fc2a 176c a856 328 8824 320 8824 fe00 ff30
  //   de0a de09 de08 fc08 d538 fe08 55e9 c865 da0d db0e db0b 12d1 16f1 b860 7f9 3d9 2d7 2d1 14e1 b85e 13df
  //   13d9 f920 510 15ef fc31 176c a878 228 8824 220 8824 fe00 ff30 de0a de09 de08 fc08 d538 fe08 55e9
  //   c887 da0d db0e db0b 12d1 16f1 b882 7f9 3d9 2d7 2d1 14e1 b880 13df 13d9 f928 518 5ef fcc0 176c a89a
  //   320 8824 328 8824 9803
  //   contents of Sprite_memory (hex, n*v repeats v):
  //   17*0 3c 70 60 60 70 3c 0 0 0 42 42 66 7e 3c 0 0 3c e 6 6 e 3c 0 0 3c 7e 66 42 42 0 0 0 3c 4*7e 3c
endmodule

module CU (
  input  CLK,
  input  RST,
  input  [15:0] Instruction,
  input  [7:0] ALU_F_IN,
  output [2:0] Reg0,
  output [2:0] Reg1,
  output [7:0] Const,
  output RF_W_nR,
  output RF_CE0,
  output RF_CE1,
  output ALU_AccuE,
  output ALU_CE,
  output [3:0] ALU_CMD,
  output RAM_WE,
  output RAM_CE,
  output RF_PTR_E,
  output CLK_QTR,
  output RF_DATAOUT_O_E,
  output IO_E,
  output [7:0] Addr,
  output ALU_F_E,
  output LNG_JMP_I,
  output LNG_JMP_R,
  output I3_TO_ALU
);

  wire Cycle0, multiplexer_2_out;
  wire [1:0] Cyclecounter_q;
  wire [2:0] OP0, OP1, register_1_q, Res;
  wire [3:3] register_1_q_2;
  wire [6:4] and_2_out;
  wire [7:0] MC_CONST8, multiplexer_1_out;
  wire [9:9] xor_1_out;
  wire [11:6] IR_q;
  wire [23:7] rom_1_data;

  Counter #(.max('h3), .width(2)) Cyclecounter (
    .Q(Cyclecounter_q), .carry(CLK_QTR), .clk(CLK), .clr(RST));  // open: load, D, count, up
  Register #(.width(16)) IR (
    .D(Instruction), .en(Cycle0), .Q({ALU_CMD, IR_q[11], Res, IR_q[7:6], OP1, OP0}), .clk(CLK), .clr(RST));
  nor nor_1 (Cycle0, Cyclecounter_q[0], Cyclecounter_q[1]);
  Multiplexer #(.width(8)) multiplexer_1 (
    .in0({{5{1'b0}}, OP0}), .in1({IR_q[7:6], OP1, OP0}), .out(multiplexer_1_out), .sel(IR_q[11]));
  Multiplexer #(.select(3)) multiplexer_2 (
    .in0(1'b0), .in1(ALU_F_IN[0]), .in2(ALU_F_IN[1]), .in3(ALU_F_IN[2]), .in4(ALU_F_IN[3]),
    .in5(ALU_F_IN[4]), .in6(ALU_F_IN[5]), .in7(ALU_F_IN[6]), .out(multiplexer_2_out), .sel(register_1_q));
  and and_1 (and_2_out[6], IR_q[7], ~IR_q[11]);  // AND_Gate
  and and_2 (and_2_out[4], ~IR_q[11], IR_q[6]);  // AND_Gate
  assign Const = rom_1_data[7] ? multiplexer_1_out : 8'bz;  // Controlled_Buffer controlled_buffer_1
  xor xor_1 (xor_1_out[9], multiplexer_2_out, register_1_q_2[3]);
  ROM #(.addrWidth(10), .dataWidth(32)) rom_1 (
    .addr({xor_1_out[9], and_2_out[6], IR_q[11], and_2_out[4], ALU_CMD, Cyclecounter_q}),
    .data({MC_CONST8, rom_1_data[23], I3_TO_ALU, LNG_JMP_R, rom_1_data[20], LNG_JMP_I, rom_1_data[18:15], ALU_F_E, rom_1_data[13], IO_E, RF_DATAOUT_O_E, rom_1_data[10], RF_PTR_E, rom_1_data[8:7], RAM_CE, RAM_WE, ALU_CE, ALU_AccuE, RF_CE1, RF_CE0, RF_W_nR}));
  assign Addr = rom_1_data[13] ? multiplexer_1_out : 8'bz;  // Controlled_Buffer controlled_buffer_2
  Multiplexer #(.select(2), .width(3)) multiplexer_3 (
    .in0(Res), .in1(OP0), .in2(OP1), .in3(3'b000), .out(Reg0), .sel({rom_1_data[10], rom_1_data[8]}));
  assign Addr = rom_1_data[20] ? MC_CONST8 : 8'bz;  // Controlled_Buffer controlled_buffer_3
  Register #(.width(4)) register_1 (
    .D(rom_1_data[18:15]), .Q({register_1_q_2[3], register_1_q}), .clk(CLK), .clr(RST));  // open: en
  Multiplexer #(.width(3)) multiplexer_4 (.in0(OP1), .in1(Res), .out(Reg1), .sel(rom_1_data[10]));

  // Notes on the sheet:
  //   (IMOPb[7],IMOPa[11],CMD1[6],CMD0[15..12], Reg_Result, Reg_Op1, Reg_Op0)
  //   IMOPb[7]
  //   IMOPa[11]
  //   CMD1[6]
  //   CMD0[15..12]
  //   OP0
  //   OP1
  //   Reg_Res
  //   CMD_const8
  //   contents of rom_1 (hex, n*v repeats v):
  //   0 0 0 5 14*0 240 241 15*0 e22 14*0 201404 105 0 0 0 1201 10*0 10e 11 0 0 10e 11 0 0 10e 11 0 0 10e
  //   11 0 0 10e 11 0 0 10e 11 0 0 10e 11 10*0 10e 11 0 0 10e 11 0 0 10e 11 0 0 10e 11 0 0 10e 11 0 0 10e
  //   11 0 0 10e 11 34*0 81000 581 0 0 8000 0 0 0 10000 0 0 0 8000 81 0 0 10000 81 0 0 0 3802 0 0 0 3001 0
  //   0 0 81 130*0 40010c 11 0 0 40010c 11 0 0 40010c 11 0 0 40010c 11 0 0 40010c 11 0 0 40010c 11 0 0
  //   40010c 11 10*0 40010c 11 0 0 40010c 11 0 0 40010c 11 0 0 40010c 11 0 0 40010c 11 0 0 40010c 11 0 0
  //   40010c 11 295*0 81 0 0 0 81
  //   Const_Enable
  //   Addr_E
  //   F_SLC_0
  //   F_SLC_1
  //   F_SLC_2
  //   F_NEG
  //   F_NEG
  //   MC_CONST8_E
  //   Reg_Select
  //   Reg_Enable
endmodule

module RF (
  input  [2:0] Addr0,
  input  [2:0] Addr1,
  input  [7:0] Data_In,
  input  W_nR,
  input  CE0,
  input  CE1,
  input  CLK,
  input  RST,
  input  PTR_E,
  input  CLK_QTR,
  output [7:0] Data_Out0,
  output [7:0] Data_Out1,
  output [7:0] PC,
  output [7:0] Pointer,
  output PC_OVF
);

  wire and_1_out, and_2_out, decoder_1_out0, decoder_1_out1, decoder_1_out2, decoder_1_out3, decoder_1_out4,
       decoder_1_out5, decoder_1_out6, decoder_1_out7, PC_OVF_t;
  wire [7:0] R1_q, R3_q, R4_q, R5_q, R6_q, R7_q, SP_2_q;

  and and_1 (and_1_out, ~Addr0[0], ~Addr0[1], ~Addr0[2], W_nR);  // AND_Gate
  Decoder #(.select(3)) decoder_1 (
    .out0(decoder_1_out0), .out1(decoder_1_out1), .out2(decoder_1_out2), .out3(decoder_1_out3),
    .out4(decoder_1_out4), .out5(decoder_1_out5), .out6(decoder_1_out6), .out7(decoder_1_out7), .sel(Addr0),
    .en(W_nR));
  and and_2 (and_2_out, ~and_1_out, CLK_QTR);  // AND_Gate
  Counter PC_0 (
    .load(decoder_1_out0), .D(Data_In), .count(and_2_out), .Q(PC), .carry(PC_OVF_t), .up(1'b1), .clk(CLK),
    .clr(RST));
  Register SP_2 (.D(Data_In), .en(decoder_1_out1), .Q(SP_2_q), .clk(CLK), .clr(RST));
  Register R1 (.D(Data_In), .en(decoder_1_out2), .Q(R1_q), .clk(CLK), .clr(RST));
  Register R3 (.D(Data_In), .en(decoder_1_out3), .Q(R3_q), .clk(CLK), .clr(RST));
  Register R4 (.D(Data_In), .en(decoder_1_out4), .Q(R4_q), .clk(CLK), .clr(RST));
  Register R5 (.D(Data_In), .en(decoder_1_out5), .Q(R5_q), .clk(CLK), .clr(RST));
  Register R6 (.D(Data_In), .en(decoder_1_out6), .Q(R6_q), .clk(CLK), .clr(RST));
  Register R7 (.D(Data_In), .en(decoder_1_out7), .Q(R7_q), .clk(CLK), .clr(RST));
  Multiplexer #(.disabled("Z"), .enable("true"), .select(3), .width(8)) multiplexer_1 (
    .in0(PC), .in1(SP_2_q), .in2(R1_q), .in3(R3_q), .in4(R4_q), .in5(R5_q), .in6(R6_q), .in7(R7_q),
    .out(Data_Out0), .sel(Addr0), .en(CE0));
  Multiplexer #(.disabled("Z"), .enable("true"), .select(3), .width(8)) multiplexer_2 (
    .in0(PC), .in1(SP_2_q), .in2(R1_q), .in3(R3_q), .in4(R4_q), .in5(R5_q), .in6(R6_q), .in7(R7_q),
    .out(Data_Out1), .sel(Addr1), .en(CE1));
  Multiplexer #(.disabled("Z"), .enable("true"), .select(3), .width(8)) multiplexer_3 (
    .in0(PC), .in1(SP_2_q), .in2(R1_q), .in3(R3_q), .in4(R4_q), .in5(R5_q), .in6(R6_q), .in7(R7_q),
    .out(Pointer), .sel(Addr1), .en(PTR_E));
  and and_3 (PC_OVF, PC_OVF_t, ~decoder_1_out0, CLK_QTR);  // AND_Gate

  // Other names for the same wires on the sheet: Q = CLK_QTR

  // Notes on the sheet:
  //   Registerfile
endmodule

module ALU (
  input  [7:0] OP0,
  input  [7:0] OP1,
  input  [3:0] CMD_15_12,
  input  [7:0] Flags_in,
  output [7:0] Result,
  output [7:0] Flags_out
);

  wire adder_1_cout, adder_2_cout, comparator_1_eq, comparator_3_eq, comparator_4_eq, E, multiplexer_2_out,
       O, R, shl_1_cout, shr_1_cout, subtractor_1_bout;
  wire [7:0] adder_1_out, adder_2_out, and_1_out, divider_1_out, divider_1_rem, Flag_Select_data,
       multiplier_1_cout, multiplier_1_out, negator_1_out, not_1_out, or_1_out, shl_1_result, shr_1_result,
       subtractor_1_out, subtractor_2_out, xnor_1_out, xor_1_out;

  ROM #(.addrWidth(4)) Flag_Select (.addr(CMD_15_12), .data(Flag_Select_data));
  Adder adder_1 (.a(OP0), .b(OP1), .out(adder_1_out), .cout(adder_1_cout));  // open: cin
  Subtractor subtractor_1 (.a(OP1), .b(OP0), .out(subtractor_1_out), .bout(subtractor_1_bout));  // open: bin
  Multiplier multiplier_1 (.a(OP0), .b(OP1), .out(multiplier_1_out), .cout(multiplier_1_cout));  // open: cin
  Divider divider_1 (.a(OP1), .b(OP0), .out(divider_1_out), .upper({8{1'b0}}), .rem(divider_1_rem));
  SHL shl_1 (.Inp(OP1), .CIn(Flags_in[1]), .Dist(OP0), .COut(shl_1_cout), .Result(shl_1_result));
  SHR shr_1 (.Inp(OP1), .CIn(Flags_in[1]), .Dist(OP0), .COut(shr_1_cout), .Result(shr_1_result));
  Negator negator_1 (.in(OP1), .out(negator_1_out));
  assign and_1_out = OP1 & OP0;  // AND_Gate and_1, 8 bits wide
  assign or_1_out = OP1 | OP0;  // OR_Gate or_1, 8 bits wide
  assign xor_1_out = OP1 ^ OP0;  // XOR_Gate xor_1, 8 bits wide
  assign not_1_out = ~OP1;  // NOT_Gate not_1, 8 bits wide
  Adder adder_2 (.a(OP0), .b(OP1), .out(adder_2_out), .cin(Flags_in[1]), .cout(adder_2_cout));
  Subtractor subtractor_2 (.a(OP1), .b(OP0), .out(subtractor_2_out), .bin(Flags_in[1]));  // open: bout
  assign xnor_1_out = ~(OP1 ^ OP0);  // XNOR_Gate xnor_1, 8 bits wide
  Comparator comparator_1 (.a({8{1'b0}}), .b(multiplier_1_cout), .eq(comparator_1_eq));  // open: gt, lt
  Comparator comparator_2 (.a({8{1'b0}}), .b(divider_1_rem), .gt(R));  // open: eq, lt
  Comparator comparator_3 (.a({8{1'b0}}), .b(OP0), .eq(comparator_3_eq));  // open: gt, lt
  Multiplexer #(.select(4), .width(8)) multiplexer_1 (
    .in0(adder_1_out), .in1(subtractor_1_out), .in2(multiplier_1_out), .in3(divider_1_out),
    .in4(shl_1_result), .in5(shr_1_result), .in6(negator_1_out), .in9(and_1_out), .in10(or_1_out),
    .in11(xor_1_out), .in12(xnor_1_out), .in13(not_1_out), .in14(adder_2_out), .in15(subtractor_2_out),
    .out(Result), .sel(CMD_15_12));  // open: in7, in8
  Multiplexer #(.select(4)) multiplexer_2 (
    .in0(adder_1_cout), .in1(subtractor_1_bout), .in2(comparator_1_eq), .in4(shl_1_cout), .in5(shr_1_cout),
    .in14(adder_2_cout), .out(multiplexer_2_out), .sel(CMD_15_12));  // open: in3, in6, in7, in8, in9, in10, in11, in12, in13, in15
  Comparator comparator_4 (.a({8{1'b0}}), .b(Result), .eq(comparator_4_eq));  // open: gt, lt
  Multiplexer #(.select(4)) multiplexer_3 (
    .in3(comparator_3_eq), .out(E), .sel(CMD_15_12));  // open: in0, in1, in2, in4, in5, in6, in7, in8, in9, in10, in11, in12, in13, in14, in15
  xor xor_2 (O, Result[7], OP1[7]);
  Multiplexer multiplexer_4 (.in0(Flags_in[0]), .in1(comparator_4_eq), .out(Flags_out[0]), .sel(Flag_Select_data[0]));
  Multiplexer multiplexer_5 (.in0(Flags_in[1]), .in1(multiplexer_2_out), .out(Flags_out[1]), .sel(Flag_Select_data[1]));
  Multiplexer multiplexer_6 (.in0(Flags_in[2]), .in1(O), .out(Flags_out[2]), .sel(Flag_Select_data[2]));
  Multiplexer multiplexer_7 (.in0(Flags_in[3]), .in1(E), .out(Flags_out[3]), .sel(Flag_Select_data[3]));
  Multiplexer multiplexer_8 (.in0(Flags_in[4]), .in1(R), .out(Flags_out[4]), .sel(Flag_Select_data[4]));

  assign Flags_out[7:5] = Flags_in[7:5];

  // Other names for the same wires on the sheet: C = Flags_in[1]; Cs = Flags_out[1]

  // Notes on the sheet:
  //   contents of Flag_Select (hex, n*v repeats v):
  //   7 3 3 19 2 2 1 0 0 5*1 7 5
  //   XXXREOCZ
  //   C-Flag
  //   E-Flag
  //   Z-flag
  //   C-flag
  //   O-flag
  //   E-flag
  //   R-flag
endmodule

module SHL (
  input  [7:0] Inp,
  input  CIn,
  input  [7:0] Dist,
  output COut,
  output [7:0] Result
);

  wire comparator_1_eq;
  wire [3:0] subtractor_1_out;
  wire [8:0] shifter_1_out;

  Subtractor #(.width(4)) subtractor_1 (.a(Dist[3:0]), .b(4'b0001), .out(subtractor_1_out));  // open: bin, bout
  Shifter #(.width(9)) shifter_1 (.in({Inp, CIn}), .\dist (subtractor_1_out), .out(shifter_1_out));
  Comparator comparator_1 (.a(Dist), .b({8{1'b0}}), .eq(comparator_1_eq));  // open: gt, lt
  Multiplexer #(.width(9)) multiplexer_1 (
    .in0(shifter_1_out), .in1({1'b0, Inp}), .out({COut, Result}), .sel(comparator_1_eq));
endmodule

module SHR (
  input  [7:0] Inp,
  input  CIn,
  input  [7:0] Dist,
  output COut,
  output [7:0] Result
);

  wire comparator_1_eq;
  wire [3:0] subtractor_1_out;
  wire [8:0] shifter_1_out;

  Subtractor #(.width(4)) subtractor_1 (.a(Dist[3:0]), .b(4'b0001), .out(subtractor_1_out));  // open: bin, bout
  Shifter #(.shift("lr"), .width(9)) shifter_1 (.in({CIn, Inp}), .\dist (subtractor_1_out), .out(shifter_1_out));
  Comparator comparator_1 (.a(Dist), .b({8{1'b0}}), .eq(comparator_1_eq));  // open: gt, lt
  Multiplexer #(.width(9)) multiplexer_1 (
    .in0(shifter_1_out), .in1({Inp, 1'b0}), .out({Result, COut}), .sel(comparator_1_eq));
endmodule
